// Logisim project Ejercicios.circ as structural Verilog: 6 circuits, main circuit equiv
module equiv (
  input  in_1,
  input  in_2,
  output Equiv
);

  xnor xnor_1 (Equiv, in_1, in_2);
endmodule

module Impl (
  input  in_1,
  input  in_2,
  output Impl
);

  wire not_1_out;

  not not_1 (not_1_out, in_1);
  or or_1 (Impl, not_1_out, in_2);
endmodule

module Ejercicio1 (
  input  P,
  input  Q,
  input  P_2,
  input  Q_2,
  input  P_3,
  input  Q_3,
  input  R,
  output out_8,
  output out_9,
  output out_10
);

  wire and_1_out, and_2_out, impl_1_impl, impl_2_impl, impl_3_impl, nand_1_out, not_1_out, not_2_out,
       or_1_out, or_2_out;

  not not_1 (not_1_out, P);
  not not_2 (not_2_out, Q);
  and and_1 (and_1_out, P_2, Q_2);
  nand nand_1 (nand_1_out, P, Q);
  or or_1 (or_1_out, not_1_out, not_2_out);
  or or_2 (or_2_out, P_2, and_1_out);
  Impl impl_1 (.in_1(P_3), .in_2(Q_3), .Impl(impl_1_impl));
  Impl impl_2 (.in_1(Q_3), .in_2(R), .Impl(impl_2_impl));
  and and_2 (and_2_out, impl_1_impl, impl_2_impl);
  Impl impl_3 (.in_1(P_3), .in_2(R), .Impl(impl_3_impl));
  equiv equiv_1 (.in_1(nand_1_out), .in_2(or_1_out), .Equiv(out_8));
  equiv equiv_2 (.in_1(P_2), .in_2(or_2_out), .Equiv(out_9));
  Impl impl_4 (.in_1(and_2_out), .in_2(impl_3_impl), .Impl(out_10));
endmodule

module Ejercicio2 (
  input  A,
  input  B,
  input  A_2,
  input  B_2,
  input  A_3,
  output out_6,
  output OR,
  output NOT
);

  wire nand_1_out, nand_2_out, nand_4_out;

  nand nand_1 (nand_1_out, A_2, A_2);
  nand nand_2 (nand_2_out, B_2, B_2);
  nand nand_3 (NOT, A_3, A_3);
  nand nand_4 (nand_4_out, A, B);
  nand nand_5 (out_6, nand_4_out, nand_4_out);
  nand nand_6 (OR, nand_1_out, nand_2_out);

  // Notes on the sheet:
  //   AND
endmodule

module Ejercicio3 (
);

  Transistor #(.\type ("n")) transistor_1 ();  // open: in, out, gate
  Transistor transistor_2 ();  // open: in, out, gate
endmodule

module Ejercicio4 (
  input  in_1,
  input  in_2,
  input  in_3,
  input  in_4,
  output out_5
);

  wire nand_1_out, nand_2_out;

  nand nand_1 (nand_1_out, in_1, in_2);
  nand nand_2 (nand_2_out, in_3, in_4);
  or or_1 (out_5, nand_1_out, nand_2_out);
endmodule
